# Fritzing sketch lightbot (saved by Fritzing 0.9.2b)
breadboards: 1

parts:
  Left_Resistor = Resistor [tolerance=±5% resistance=220 package=THT]
  Left_Photoresistor = PHOTOCELL [package=photocell]
  Right_Photoresistor = PHOTOCELL [package=photocell]
  Right_Resistor = Resistor [tolerance=±5% resistance=220 package=THT]
  Left_MOSFET = Basic FET N-Channel [package="D2Pak [SMD]"]
  Right_MOSFET = Basic FET N-Channel [package="D2Pak [SMD]"]
  Arduino = Arduino Uno (Rev3)
  Left_Motor = DC Motor
  Right_Motor = DC Motor
  Battery = Battery block 9V

nets (from the schematic view):
  N1: Left_Resistor.Pin_0, Left_Photoresistor.P$2, Arduino.A0
  N2: Left_Resistor.Pin_1, Right_Resistor.Pin_0, Left_MOSFET.source, Right_MOSFET.source, Arduino.GND, Battery.-
  N3: Left_Photoresistor.P$1, Right_Photoresistor.P$2, Arduino.5V
  N4: Right_Photoresistor.P$1, Right_Resistor.Pin_1, Arduino.A1
  N5: Left_MOSFET.Gate, Arduino.D5_PWM
  N6: Left_MOSFET.drain, Left_Motor.pin_2
  N7: Right_MOSFET.Gate, Arduino.D6_PWM
  N8: Right_MOSFET.drain, Right_Motor.pin_2
  N9: Arduino.VIN, Left_Motor.pin_1, Right_Motor.pin_1, Battery.+
